# Fritzing sketch BikePixel sketch (saved by Fritzing 0.9.3b)
circuit board: 8.46667cm x 5.64444cm
breadboards: 1

parts:
  S1 = Pushbutton [package="[THT]"]
  S2 = Pushbutton [package="[THT]"]
  S3 = Pushbutton [package="[THT]"]
  R1 = Resistor [tolerance=±5% resistance=100k package=THT]
  Componente1 = Arduino Uno (Rev3)
  VCC2 = 4 x AAA Battery Mount
  Componente2 = NeoPixel NeoMatrix 8x8 [part_number=1487]
  J1 = male pin header, 6 pins [form="♂ (male)"]
  J2 = female pin header, 3 pins [form="♀ (female)"]
  C1 = Tantalum Capacitor [capacitance=1μF package="100 mil [THT, tantalum]"]

nets:
  5V: S1.Pin_1, S1.Pin_2, S2.Pin_1, S2.Pin_2, S3.Pin_1, S3.Pin_2, Componente1.D6_PWM, Componente1.5V, Componente2.VDD, J1.pin1, J1.pin5, J2.pin3, C1.+
  N1: S1.Pin_3, S1.Pin_4, S2.Pin_3, S2.Pin_4, S3.Pin_3, S3.Pin_4, R1.Pin_1, Componente1.D4, Componente1.D5_PWM, J1.pin3, J1.pin4
  GND: R1.Pin_0, Componente1.GND, VCC2.-, Componente2.GND, J1.pin2, J2.pin2, C1.-
  N2: Componente1.D7, Componente2.IN, J1.pin6, J2.pin1
  N3: Componente1.VIN, VCC2.+

notes:
  Use 6 AAA battery holder

custom parts:
  NeoPixel NeoMatrix 8x8: Put on your sunglasses before wiring up this LED matrix - 64 eye-blistering RGB LEDs adorn the NeoMatrix for a blast of configurable color. Arranged in an 8x8 matrix, each pixel is individually addressable. Only one microcontroller pin is required to control all the LEDs, and you get 24 bit color for each LED.
