# Fritzing sketch sketch pcb (saved by Fritzing 0.9.3b)
circuit board: 5.99999cm x 2.5cm
breadboards: 1

parts:
  mode = Pushbutton [package="[THT]"]
  Brg- = Pushbutton [package="[THT]"]
  Brg+ = Pushbutton [package="[THT]"]
  J2 = female pin header, 3 pins [form="♀ (female)"]
  R1 = Resistor [tolerance=±5% resistance=470 package=THT]
  R2 = Resistor [tolerance=±5% resistance=100k package=THT]
  R3 = Resistor [tolerance=±5% resistance=100k package=THT]
  R1_2 = Resistor [tolerance=±5% resistance=10k package=THT]
  J1 = male pin header, 6 pins [form="♂ (male)"]

nets:
  N1: mode.Pin_1, mode.Pin_2, Brg-.Pin_1, Brg-.Pin_2, Brg+.Pin_1, Brg+.Pin_2, J2.pin1, J1.pin2
  N2: mode.Pin_3, mode.Pin_4, R1_2.Pin_0, J1.pin6
  N3: Brg-.Pin_3, Brg-.Pin_4, R3.Pin_1, J1.pin5
  N4: Brg+.Pin_3, Brg+.Pin_4, R2.Pin_1, J1.pin4
  N5: J2.pin2, R2.Pin_0, R3.Pin_0, R1_2.Pin_1, J1.pin3
  N6: J2.pin3, R1.Pin_1
  N7: R1.Pin_0, J1.pin1

notes:
  To battery + 1000uF/6.3
  BikePixels.com
  rear v0.1
