# Fritzing sketch sketch protoboard (saved by Fritzing 0.9.3b)
circuit board: 8.46667cm x 5.64444cm
breadboards: 1

parts:
  mode = Pushbutton [package="[THT]"]
  Brg- = Pushbutton [package="[THT]"]
  Brg+ = Pushbutton [package="[THT]"]
  R1 = Resistor [tolerance=±5% resistance=10k package=THT]
  Componente1 = Arduino Uno (Rev3)
  VCC2 = 4 x AAA Battery Mount
  Componente2 = NeoPixel NeoMatrix 8x8 [part_number=1487]
  J1 = male pin header, 6 pins [form="♂ (male)"]
  J2 = female pin header, 3 pins [form="♀ (female)"]
  C1 = Tantalum Capacitor [capacitance=1μF package="100 mil [THT, tantalum]"]
  R2 = Resistor [tolerance=±5% resistance=470 package=THT]
  R3 = Resistor [tolerance=±5% resistance=10k package=THT]
  R4 = Resistor [tolerance=±5% resistance=10k package=THT]

nets:
  N1: mode.Pin_1, mode.Pin_2, R1.Pin_0, Componente1.D4, J1.pin1
  5V: mode.Pin_3, mode.Pin_4, Brg-.Pin_1, Brg-.Pin_2, Brg+.Pin_1, Brg+.Pin_2, Componente1.5V, Componente2.VDD, J1.pin3, J2.pin3, C1.+
  N2: Brg-.Pin_3, Brg-.Pin_4, Brg+.Pin_3, Brg+.Pin_4, Componente1.D5_PWM, Componente1.D6_PWM, J1.pin4, J1.pin5, R3.Pin_1, R4.Pin_1
  GND: R1.Pin_1, Componente1.GND, VCC2.-, Componente2.GND, J1.pin2, J2.pin2, C1.-, R3.Pin_0, R4.Pin_0
  N3: Componente1.D7, J1.pin6, R2.Pin_0
  N4: Componente1.VIN, VCC2.+
  N5: Componente2.IN, J2.pin1, R2.Pin_1

notes:
  Use 6 AAA battery holder
  Note that this Matrix schema version is outdated. 5V and GDD central pins are missing. You should use them to power the matrix.

custom parts:
  NeoPixel NeoMatrix 8x8: Put on your sunglasses before wiring up this LED matrix - 64 eye-blistering RGB LEDs adorn the NeoMatrix for a blast of configurable color. Arranged in an 8x8 matrix, each pixel is individually addressable. Only one microcontroller pin is required to control all the LEDs, and you get 24 bit color for each LED.
