# Fritzing sketch bikepixel-L-connection-breadboard (saved by Fritzing 0.9.4)

parts:
  TP1 = TP4056 [chip_label=TP4056 package="DIP (Dual Inline) [THT]"]
  Nano = Arduino Nano (Rev3.0)
  U1 = Battery Holders [package=lipo-1100mAh]
  Step-up = Pololu 5V Step-Up Regulator
  Componente3 = NeoPixel NeoMatrix 8x8 [part_number=1487]
  BP_L_PCB1 = Bike Pixel L PCB [package="DIP (Dual Inline) [THT]"]

nets:
  N1: TP1.pin3, Step-up.VIN
  N2: TP1.pin4, U1.+, BP_L_PCB1.B+
  N3: TP1.pin5, U1.-
  N4: TP1.pin6, Step-up.GND, BP_L_PCB1.GND#2
  N5: Nano.GND, BP_L_PCB1.GND#7
  N6: Nano.D3, BP_L_PCB1.mode
  N7: Nano.D4, BP_L_PCB1.color
  N8: Nano.D5, BP_L_PCB1.effect
  N9: Nano.D6, BP_L_PCB1.Din
  N10: Nano.5V, BP_L_PCB1.5Vout#5
  N11: Nano.A6, BP_L_PCB1.B+_out
  N12: Step-up.VOUT, BP_L_PCB1.5Vin
  N13: Componente3.IN, BP_L_PCB1.Dout
  N14: Componente3.VDD, BP_L_PCB1.5Vout#11
  N15: Componente3.GND, BP_L_PCB1.GND#13

custom parts:
  TP4056: A DIP stand-in part for whatever IC you want. With 6 pins on a 300mil dual inline package (DIP) footprint.
  NeoPixel NeoMatrix 8x8: Put on your sunglasses before wiring up this LED matrix - 64 eye-blistering RGB LEDs adorn the NeoMatrix for a blast of configurable color. Arranged in an 8x8 matrix, each pixel is individually addressable. Only one microcontroller pin is required to control all the LEDs, and you get 24 bit color for each LED.
  Bike Pixel L PCB: Bike Pixel L PCB with push buttons and conections
