# Fritzing sketch bike_pixel_front_pcb (saved by Fritzing 0.9.3b)
circuit board: 2.99999cm x 2.99999cm
breadboards: 1

parts:
  R2 = Resistor [tolerance=±5% resistance=220 package=THT]
  R1 = Resistor [tolerance=±5% resistance=220 package=THT]
  J1 = female pin header, 7 pins [form="♀ (female)"]
  J2 = female pin header, 3 pins [form="♀ (female)"]
  Mode = Momentary Switch Vertical [package=tactile-pth]
  Color = Momentary Switch Vertical [package=tactile-pth]
  R3 = Resistor [tolerance=±5% resistance=220 package=THT]
  on/off = Toggle Switch Vertical [package=THT]

nets:
  N1: R2.Pin_0, R1.Pin_0, J1.pin4, J2.pin2
  N2: R2.Pin_1, Color.2
  N3: R1.Pin_1, Mode.4
  N4: J1.pin1, Color.4
  N5: J1.pin2, R3.Pin_1
  N6: J1.pin3, J2.pin1, Mode.3, Color.1
  N7: J1.pin5, on/off.COM
  N8: J1.pin6, on/off.L1
  N9: J1.pin7, Mode.2
  N10: J2.pin3, R3.Pin_0

notes:
  Bike Pixel front v1
  BikePixels.com
  K.Stopa © 2020
  CERN OHL v1.2 lisence

custom parts:
  Momentary Switch Vertical: Momentary Switch Button commonly used for reset or general input. Spark Fun Electronics SKU : COM-00097
  Toggle Switch Vertical: Vertical Toggle Switch
