# Fritzing sketch bikepixel rear sketch pcb (saved by Fritzing 0.9.3b)
circuit board: 8.00001cm x 2.5cm
breadboards: 1

parts:
  mode = Pushbutton [package="[THT]"]
  Color = Pushbutton [package="[THT]"]
  Effect = Pushbutton [package="[THT]"]
  R1 = Resistor [tolerance=±5% resistance=470 package=THT]
  R2 = Resistor [tolerance=±5% resistance=100k package=THT]
  R3 = Resistor [tolerance=±5% resistance=100k package=THT]
  R4 = Resistor [tolerance=±5% resistance=10k package=THT]
  Power = female pin header, 3 pins [form="♀ (female)"]
  on/off = Toggle Switch Vertical [package=THT]
  R5 = Resistor [tolerance=±5% resistance=10k package=THT]
  R6 = Resistor [tolerance=±5% resistance=10k package=THT]
  Matrix = female pin header, 3 pins [form="♀ (female)"]
  Main = male pin header, 7 pins [form="♂ (male)"]

nets:
  N1: mode.Pin_1, mode.Pin_2, on/off.COM, Main.pin6
  N2: mode.Pin_3, mode.Pin_4, R4.Pin_0, Main.pin4
  N3: Color.Pin_3, Color.Pin_4, R3.Pin_1, Main.pin2
  N4: Effect.Pin_1, Effect.Pin_2, Matrix.pin2
  N5: Effect.Pin_3, Effect.Pin_4, R2.Pin_1, Main.pin3
  N6: R1.Pin_0, Main.pin1
  N7: R1.Pin_1, Matrix.pin3
  N8: R2.Pin_0, R3.Pin_0, R4.Pin_1, Power.pin1, R6.Pin_0, Matrix.pin1, Main.pin7
  N9: Power.pin2, on/off.L2
  N10: Power.pin3, R5.Pin_0
  N11: R5.Pin_1, R6.Pin_1, Main.pin5

notes:
  To battery + 1000uF/6.3
  Bike Pixel rear v0.5
  BikePixels.com
  OSHWA PL000002

custom parts:
  Toggle Switch Vertical: Vertical Toggle Switch
