# Fritzing sketch bikepixel rear sketch protoboard (saved by Fritzing 0.9.3b)
circuit board: 8.46667cm x 5.64444cm
breadboards: 1

parts:
  mode = Pushbutton [package="[THT]"]
  Brg- = Pushbutton [package="[THT]"]
  Brg+ = Pushbutton [package="[THT]"]
  R1 = Resistor [tolerance=±5% resistance=10k package=THT]
  Componente2 = NeoPixel NeoMatrix 8x8 [part_number=1487]
  J1 = male pin header, 6 pins [form="♂ (male)"]
  J2 = female pin header, 3 pins [form="♀ (female)"]
  C1 = Tantalum Capacitor [capacitance=1μF package="100 mil [THT, tantalum]"]
  R2 = Resistor [tolerance=±5% resistance=470 package=THT]
  R3 = Resistor [tolerance=±5% resistance=10k package=THT]
  R4 = Resistor [tolerance=±5% resistance=10k package=THT]
  Part1 = Arduino Nano (Rev3.0)
  VCC2 = 4 x AAA Battery Mount

nets:
  N1: mode.Pin_1, mode.Pin_2, R1.Pin_0, J1.pin1, Part1.D2
  N2: mode.Pin_3, mode.Pin_4, Brg-.Pin_1, Brg-.Pin_2, Brg+.Pin_1, Brg+.Pin_2, J1.pin5, C1.+, Part1.5V
  N3: Brg-.Pin_3, Brg-.Pin_4, Brg+.Pin_3, Brg+.Pin_4, J1.pin2, J1.pin3, R3.Pin_1, R4.Pin_1, Part1.D3, Part1.D4
  GND: R1.Pin_1, Componente2.GND, J1.pin4, J2.pin2, C1.-, R3.Pin_0, R4.Pin_0, Part1.GND, VCC2.-
  N4: Componente2.OUT, J2.pin1, R2.Pin_1
  N5: Componente2.VDD, J2.pin3
  N6: J1.pin6, R2.Pin_0, Part1.D5
  N7: Part1.VIN, VCC2.+

notes:
  Use 6 AAA battery holder or connect to an external USB battery
  Note that this Matrix schema version is outdated. 5V and GDD central pins are missing. You should use them to power the matrix.

custom parts:
  NeoPixel NeoMatrix 8x8: Put on your sunglasses before wiring up this LED matrix - 64 eye-blistering RGB LEDs adorn the NeoMatrix for a blast of configurable color. Arranged in an 8x8 matrix, each pixel is individually addressable. Only one microcontroller pin is required to control all the LEDs, and you get 24 bit color for each LED.
