# Fritzing sketch sketch pcb (saved by Fritzing 0.9.3b)
circuit board: 8.00001cm x 2.5cm
breadboards: 1

parts:
  mode = Pushbutton [package="[THT]"]
  Brg- = Pushbutton [package="[THT]"]
  Brg+ = Pushbutton [package="[THT]"]
  R1 = Resistor [tolerance=±5% resistance=470 package=THT]
  R2 = Resistor [tolerance=±5% resistance=100k package=THT]
  R3 = Resistor [tolerance=±5% resistance=100k package=THT]
  R4 = Resistor [tolerance=±5% resistance=10k package=THT]
  Power = female pin header, 3 pins [form="♀ (female)"]
  on/off = Toggle Switch Vertical [package=THT]
  R5 = Resistor [tolerance=±5% resistance=10k package=THT]
  R6 = Resistor [tolerance=±5% resistance=10k package=THT]
  Main = male pin header, 9 pins [form="♂ (male)"]
  Matrix = female pin header, 3 pins [form="♀ (female)"]

nets:
  N1: mode.Pin_1, mode.Pin_2, Brg-.Pin_1, Brg+.Pin_1, Brg+.Pin_2, Main.pin3, Matrix.pin1
  N2: mode.Pin_3, mode.Pin_4, R4.Pin_0, Main.pin6
  N3: Brg-.Pin_3, Brg-.Pin_4, R3.Pin_1, Main.pin5
  N4: Brg+.Pin_3, Brg+.Pin_4, R2.Pin_1, Main.pin4
  N5: R1.Pin_0, Main.pin1
  N6: R1.Pin_1, Matrix.pin3
  N7: R2.Pin_0, R6.Pin_1, Main.pin2, Matrix.pin2
  N8: R3.Pin_0, R4.Pin_1
  N9: Power.pin1, Main.pin9
  N10: Power.pin2, on/off.L2
  N11: Power.pin3, R5.Pin_0
  N12: on/off.COM, Main.pin8
  N13: R5.Pin_1, R6.Pin_0, Main.pin7

notes:
  To battery + 1000uF/6.3
  Bike Pixel rear v0.5
  K.Stopa (c) 2020
  BikePixels.com

custom parts:
  Toggle Switch Vertical: Vertical Toggle Switch
